# Fritzing sketch Ultrasonic-Sensor-HC-SR04-With-Buzzer (saved by Fritzing 0.9.3b)
breadboards: 1

parts:
  hc-sr1 = hc-sr04  # not connected
  Componente1 = Arduino Uno (Rev3) - ICSP
  J1 = Piezo Speaker
  LED1 = LED - 3mm [color="Red (633nm)" package="3 mm [THT]"]
  R1 = Resistor [tolerance=±5% resistance=220 package=THT]

nets:
  N1: Componente1.D11_PWM/MOSI, J1.pin2
  N2: Componente1.D12/MISO, R1.Pin_0
  N3: Componente1.D13/SCK, LED1.anode
  N4: Componente1.GND, J1.pin1
  N5: LED1.cathode, R1.Pin_1
