# Fritzing sketch nodeMCU_dht22 (saved by Fritzing 0.9.3b)
breadboards: 1

parts:
  Teensy_3_1 = Teensy 3.1
  RHT1 = Humidity and Temperature Sensor RHT03

nets:
  N1: Teensy_3_1.GND, RHT1.GND_1
  N2: Teensy_3_1.D0, RHT1.Data-signal
  N3: Teensy_3_1.D9, RHT1.Vcc
